# Fritzing sketch msp430-remote_prototype (saved by Fritzing 0.9.1b)

parts:
  R1 = Trimmer Potentiometer [maximum_resistance=10kΩ package=THT]
  R2 = Trimmer Potentiometer [maximum_resistance=10kΩ package=THT]
  R3 = Trimmer Potentiometer [maximum_resistance=10kΩ package=THT]
  Launchpad1 = TI Launchpad MSP430G2
  NRF24L1 = NRF24L01

nets:
  N1: R1.leg1, R2.leg1, R3.leg1, Launchpad1.p20
  N2: R1.wiper, Launchpad1.p2
  N3: R1.leg2, R2.leg2, R3.leg2, Launchpad1.p1
  N4: R2.wiper, Launchpad1.p5
  N5: R3.wiper, Launchpad1.p6
  N6: Launchpad1.p10, NRF24L1.IRQ
  N7: Launchpad1.p9, NRF24L1.CSN
  N8: Launchpad1.p8, NRF24L1.CE
  N9: Launchpad1.p7, NRF24L1.SCK
  N10: Launchpad1.p14, NRF24L1.MISO
  N11: Launchpad1.p15, NRF24L1.MOSI

custom parts:
  NRF24L01: NRF24L01 module
